# Fritzing sketch v0 (saved by Fritzing 0.9.6b)
breadboards: 1

parts:
  Part1 = Arduino Nano (Rev3.0)

nets:
  GND: Part1.GND
  XSHUT: Part1.D2, Part1.D3
  Din: Part1.D4
  RESET: Part1.D8
  CS-SD: Part1.D9
  CS-LD: Part1.D10
  MOSI: Part1.D11/MOSI
  MISO: Part1.D12/MISO
  +5V/BL/VIN: Part1.5V
  SCL: Part1.A5
  SDA: Part1.A4
  SCK: Part1.D13/SCK

notes:
  ROBOT LCD
  WS2812B
  VL53LXX-V2
