# Fritzing sketch V1 (saved by Fritzing 0.9.6b)

parts:
  Part1 = Arduino Nano (Rev3.0)

nets:
  GND: Part1.GND
  RESET: Part1.D8
  D/C-LD: Part1.D9
  CS-LD: Part1.D10
  MOSI: Part1.D11/MOSI
  MISO: Part1.D12/MISO
  +5V/BL: Part1.5V
  SCK: Part1.D13/SCK

notes:
  ROBOT LCD
