# Fritzing sketch v2 (saved by Fritzing 0.9.6b)
breadboards: 1

parts:
  R1 = Resistor [tolerance=±5% power=0.25W resistance=220 package=THT]
  R2 = Resistor [tolerance=±5% power=0.25W resistance=220 package=THT]
  R3 = Resistor [tolerance=±5% power=0.25W resistance=220 package=THT]
  R4 = Resistor [tolerance=±5% power=0.25W resistance=220 package=THT]
  R5 = Resistor [tolerance=±5% power=0.25W resistance=220 package=THT]
  LED1 = LED - 5mm [color="Red (633nm)" current=0.030 package="5 mm [THT]"]
  LED2 = LED - 5mm [color="Red (633nm)" current=0.030 package="5 mm [THT]"]
  LED3 = LED - 5mm [color="Red (633nm)" current=0.030 package="5 mm [THT]"]
  LED4 = LED - 5mm [color="Red (633nm)" current=0.030 package="5 mm [THT]"]
  LED5 = LED - 5mm [color="Red (633nm)" current=0.030 package="5 mm [THT]"]
  S2 = Pushbutton [package="[THT]"]
  S3 = Pushbutton [package="[THT]"]
  S4 = Pushbutton [package="[THT]"]
  S5 = Pushbutton [package="[THT]"]
  S6 = Pushbutton [package="[THT]"]
  Part1 = Arduino Nano (Rev3.0)
  Part2 = Arduino Mega 2560 (Rev3)  # not connected

nets:
  N1: R1.Pin_0, Part1.D10
  N2: R1.Pin_1, LED1.anode
  N3: R2.Pin_0, Part1.D8
  N4: R2.Pin_1, LED4.anode
  N5: R3.Pin_0, Part1.D12/MISO
  N6: R3.Pin_1, LED3.anode
  N7: R4.Pin_0, Part1.D11/MOSI
  N8: R4.Pin_1, LED5.anode
  N9: R5.Pin_0, Part1.D9
  N10: R5.Pin_1, LED2.anode
  N11: LED1.cathode, LED2.cathode, LED3.cathode, LED4.cathode, LED5.cathode, S2.Pin_3, S2.Pin_4, S3.Pin_3, S3.Pin_4, S4.Pin_3, S4.Pin_4, S5.Pin_3, S5.Pin_4, S6.Pin_1, S6.Pin_2, Part1.GND
  N12: S2.Pin_1, S2.Pin_2, Part1.D4
  N13: S3.Pin_1, S3.Pin_2, Part1.D6
  N14: S4.Pin_1, S4.Pin_2, Part1.D3
  N15: S5.Pin_1, S5.Pin_2, Part1.D5
  N16: S6.Pin_3, S6.Pin_4, Part1.D2
