# Fritzing sketch v2 (saved by Fritzing 0.9.6b)
breadboards: 1

parts:
  R1 = Resistor [tolerance=±5% power=0.25W resistance=220 package=THT]
  R2 = Resistor [tolerance=±5% power=0.25W resistance=220 package=THT]
  R3 = Resistor [tolerance=±5% power=0.25W resistance=220 package=THT]
  R4 = Resistor [tolerance=±5% power=0.25W resistance=220 package=THT]
  R5 = Resistor [tolerance=±5% power=0.25W resistance=220 package=THT]
  LED1 = LED - 5mm [color="Red (633nm)" current=0.030 package="5 mm [THT]"]
  LED2 = LED - 5mm [color="Red (633nm)" current=0.030 package="5 mm [THT]"]
  LED3 = LED - 5mm [color="Red (633nm)" current=0.030 package="5 mm [THT]"]
  LED4 = LED - 5mm [color="Red (633nm)" current=0.030 package="5 mm [THT]"]
  LED5 = LED - 5mm [color="Red (633nm)" current=0.030 package="5 mm [THT]"]
  S2 = Pushbutton [package="[THT]"]
  S3 = Pushbutton [package="[THT]"]
  S4 = Pushbutton [package="[THT]"]
  S5 = Pushbutton [package="[THT]"]
  S6 = Pushbutton [package="[THT]"]
  Part2 = Arduino Mega 2560 (Rev3)

nets:
  N1: R1.Pin_0, Part2.D16_PWM/TX2
  N2: R1.Pin_1, LED1.anode
  N3: R2.Pin_0, Part2.D18/TX1
  N4: R2.Pin_1, LED4.anode
  N5: R3.Pin_0, Part2.D14/TX3
  N6: R3.Pin_1, LED3.anode
  N7: R4.Pin_0, Part2.D15/RX3
  N8: R4.Pin_1, LED5.anode
  N9: R5.Pin_0, Part2.D17_PWM/RX2
  N10: R5.Pin_1, LED2.anode
  N11: LED1.cathode, LED2.cathode, LED3.cathode, LED4.cathode, LED5.cathode, S2.Pin_3, S2.Pin_4, S3.Pin_3, S3.Pin_4, S4.Pin_3, S4.Pin_4, S5.Pin_3, S5.Pin_4, S6.Pin_1, S6.Pin_2
  N12: S2.Pin_1, S2.Pin_2, Part2.D11_PWM
  N13: S3.Pin_1, S3.Pin_2, Part2.D13_PWM
  N14: S4.Pin_1, S4.Pin_2, Part2.D10_PWM
  N15: S5.Pin_1, S5.Pin_2, Part2.D12_PWM
  N16: S6.Pin_3, S6.Pin_4, Part2.D9_PWM
  +5V/BL: Part2.5V
  D/C-LD: Part2.D48
  RESET: Part2.D49
  MISO: Part2.D50
  MOSI: Part2.D51
  SCK: Part2.D52
  CS-LD: Part2.D53
  GND: Part2.GND

notes:
  ROBOT LCD
