# Fritzing sketch phone (saved by Fritzing 0.9.6b)
breadboards: 1

parts:
  R1 = Resistor [tolerance=±5% power=0.25W resistance=330k package=THT]
  D1 = Rectifier Diode [part_number=1N4001 package="300 mil [THT]"]
  D2 = Rectifier Diode [part_number=1N4001 package="300 mil [THT]"]
  D3 = Rectifier Diode [part_number=1N4001 package="300 mil [THT]"]
  R6 = Resistor [tolerance=±5% power=0.25W resistance=330k package=THT]
  R7 = Resistor [tolerance=±5% power=0.25W resistance=330k package=THT]
  R8 = Resistor [tolerance=±5% power=0.25W resistance=330k package=THT]
  R9 = Resistor [tolerance=±5% power=0.25W resistance=2.2k package=THT]
  S1 = Toggle Switch [package=THT]
  Part1 = Arduino Nano (Rev3.0)
  microSD1 = MicroSD Card Module
  S3 = Pushbutton [package=THT]

nets:
  GND/GREEN: R1.Pin_0, R6.Pin_0, R7.Pin_0, R8.Pin_0, Part1.GND, microSD1.GND, S3.leg1
  R1: R1.Pin_1, Part1.D8
  C1: D1.cathode
  N1: D1.anode, Part1.D2
  C2: D2.cathode
  N2: D2.anode, Part1.D4
  C3: D3.cathode
  N3: D3.anode, Part1.D3
  R3: R6.Pin_1, Part1.D6
  R2: R7.Pin_1, Part1.D7
  R4: R8.Pin_1, Part1.D5
  N4: R9.Pin_0, S1.L1
  RED: R9.Pin_1
  N5: S1.COM, Part1.D9
  SPK: S1.L2
  N6: Part1.D10, microSD1.CS
  N7: Part1.D11/MOSI, microSD1.MOSI
  N8: Part1.D12/MISO, microSD1.MISO
  5V: Part1.5V, microSD1.VCC
  N9: Part1.A0, S3.leg0
  N10: Part1.D13/SCK, microSD1.SCK

notes:
  PHONE BUTTONS
  HANDPIECE
  HANG BUTTON
