# Fritzing sketch rfid_eye (saved by Fritzing 0.9.6b)
breadboards: 1

parts:
  Part1 = Arduino Nano (Rev3.0)

nets:
  RST: Part1.D9
  SDA: Part1.D10, Part1.A4
  MOSI: Part1.D11/MOSI
  MISO: Part1.D12/MISO
  GND: Part1.GND
  VCC: Part1.5V
  SCK: Part1.A5, Part1.D13/SCK
  3V3: Part1.3V3

notes:
  OLED screen 128x32 I2C
  RFID-RC522
